# Fritzing sketch Pantalla-oled (saved by Fritzing 0.9.3b)

parts:
  Part1 = Arduino Uno (Rev3)
  OLED1 = OLED 128x64 I2C Monochrome Display

nets:
  N1: Part1.A4/SDA, OLED1.SDA
  N2: Part1.A5/SCL, OLED1.SCK
  5V: Part1.5V, OLED1.VDD
  GND: Part1.GND, OLED1.GND
